# Fritzing sketch main_diagram (saved by Fritzing 1.0.5)
breadboards: 1

parts:
  DHT22_/_3_3V = DHT22 module
  Raspberry_Pi_4_Model_B = Raspberry Pi 4B
  HC-SR501_PIR_sensor_/_5V = HC-SR501 Body Sensor Module
  MH-Z19C1 = MH-Z19C

nets:
  N1: DHT22_/_3_3V.+, Raspberry_Pi_4_Model_B.3V3
  N2: DHT22_/_3_3V.Out, Raspberry_Pi_4_Model_B.GPIO4
  GND: DHT22_/_3_3V.-, Raspberry_Pi_4_Model_B.GND, HC-SR501_PIR_sensor_/_5V.GND, MH-Z19C1.GND
  5V: Raspberry_Pi_4_Model_B.5V, HC-SR501_PIR_sensor_/_5V.VCC, MH-Z19C1.Vin
  N3: Raspberry_Pi_4_Model_B.GPIO14, MH-Z19C1.Rx
  N4: Raspberry_Pi_4_Model_B.GPIO15, MH-Z19C1.Tx
  N5: Raspberry_Pi_4_Model_B.GPIO17, HC-SR501_PIR_sensor_/_5V.OUT

notes:
  <--- 3.3 Volts
  <--- 5 Volts
  Although the connector type is different, both the pin header and wafer versions of the MH-Z19C, they share the same electrical pinout and function; only the physical layout and wire orientation differ

custom parts:
  DHT22 module: DHT22 module. Pins VCC Data GND.
  HC-SR501 Body Sensor Module: Pyroelectric Infrared PIR Motion Sensor Detector Module
  MH-Z19C: CO2-Sensor https://www.winsen-sensor.com/
